# Fritzing sketch TemperatureMonitor (saved by Fritzing 0.8.5b)
breadboards: 1

parts:
  DHT11 = DHT11 Humitidy and Temperature Sensor
  R1 = Resistor [tolerance=±5% resistance=10k package=THT]
  Raspberry_Pi_B_rev1 = Raspberry Pi B rev2

nets:
  VDD: DHT11.VDD, R1.Pin_0, Raspberry_Pi_B_rev1.3V3
  N1: DHT11.DATA, R1.Pin_1, Raspberry_Pi_B_rev1.GPIO_4
  N2: DHT11.GND, Raspberry_Pi_B_rev1.GPIO_3

custom parts:
  DHT11 Humitidy and Temperature Sensor: DHT11 Humidity and Temperature Sensor
